# Fritzing sketch ir-decoder (saved by Fritzing 0.8.7b)
circuit board: 8.46667cm x 5.64444cm
breadboards: 1

parts:
  Part1 = Arduino Uno (Rev3)
  IR1 = TSOP312.., 314.. [package=THT]

nets:
  N1: Part1.D12/MISO, IR1.Data
  GND: Part1.GND, IR1.GND
  N2: Part1.5V, IR1.Vs
